# Fritzing sketch blink_with_pushbutton (saved by Fritzing 0.9.3b)
breadboards: 1

parts:
  Componente1 = Arduino Uno (Rev3)
  LED1 = LED - 5mm [color="Red (633nm)" package="5 mm [THT]"]
  R1 = Resistor [tolerance=±5% resistance=220 package=THT]
  S1 = Pushbutton [package="[THT]"]

nets:
  N1: Componente1.D13/SCK, LED1.anode
  N2: Componente1.GND, S1.Pin_3, S1.Pin_4
  N3: LED1.cathode, R1.Pin_1
  N4: R1.Pin_0, S1.Pin_1, S1.Pin_2

// code stored in the sketch: code.ino
void setup() {
	int pino = 13;
}

void loop() {
	pinMode(pino, HIGH);
}
